# Fritzing sketch NanoChess (saved by Fritzing 0.9.4)
breadboards: 1

parts:
  Part1 = Arduino Nano (Rev3.0)
  Part2 = Arduino Nano (Rev3.0)
  OLED1 = OLED 128x64 I2C Monochrome Display VDD-GND
  S1 = Pushbutton [package="[SMD]"]

nets:
  N1: Part1.RESET, Part2.RESET, S1.Pin_3, S1.Pin_4
  GND: Part1.GND, Part2.GND, Part2.D12/MISO, OLED1.GND, S1.Pin_1, S1.Pin_2
  N2: Part1.D6, Part2.A2
  N3: Part1.D7, Part2.A3
  5V: Part1.5V, Part2.5V, OLED1.VDD
  N4: Part1.A5, Part2.A6, OLED1.SCK
  N5: Part1.A4, Part2.A5, OLED1.SDA

notes:
  Black (k)
  White (K)

custom parts:
  OLED 128x64 I2C Monochrome Display VDD-GND: OLED 128x64 I2C Monochrome Display. Note: there are two variants of this part, this one is the VDD GND SCK SDA variant. The other is GND VDD SCK SDA. Make sure you select the part that matches your module as using the incorrect part will probably destroy your module! In addition the mounting holes are marked on silkscreen but not by default drilled. If you want drilled mounting holes, copy a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
